// Logisim project cpu.circ as structural Verilog: 2 circuits, main circuit main
module main (
);

  wire clock_1_out;
  wire [4:0] bit_extender_1_out, bit_extender_2_out;
  wire [15:0] counter_1_q;
  wire [31:0] registers_1_reg_out_0, registers_1_reg_out_1, rom_1_data, undriven;

  Clock clock_1 (.out(clock_1_out));
  Counter #(.max('hffff), .width(16)) counter_1 (
    .clk(clock_1_out), .Q(counter_1_q));  // open: clr, load, up, count, D, carry
  ROM #(.addrWidth(16), .dataWidth(32)) rom_1 (.addr(counter_1_q), .data(rom_1_data));
  Bit_Extender #(.in_width(11), .out_width(5)) bit_extender_1 (.in(rom_1_data[15:5]), .out(bit_extender_1_out));
  Bit_Extender #(.in_width(11), .out_width(5)) bit_extender_2 (.in(rom_1_data[26:16]), .out(bit_extender_2_out));
  Decoder #(.enable("false"), .select(5)) decoder_1 (.sel(rom_1_data[4:0]));  // open: out0, out1, out2, out3, out4, out5, out6, out7, out8, out9, out10, out11, out12, out13, out14, out15, out16, out17, out18, out19, out20, out21, out22, out23, out24, out25, out26, out27, out28, out29, out30, out31
  registers registers_1 (
    .reg_in(undriven), .reg_load_0(bit_extender_1_out), .reg_load_1(bit_extender_2_out), .clock(clock_1_out),
    .reg_save(rom_1_data[31:27]), .reg_out_0(registers_1_reg_out_0), .reg_out_1(registers_1_reg_out_1));
endmodule

module registers (
  input  clock,
  input  [4:0] reg_save,
  input  [31:0] reg_in,
  input  [4:0] reg_load_0,
  input  [4:0] reg_load_1,
  output [31:0] reg_out_0,
  output [31:0] reg_out_1
);

  wire decoder_1_out1, decoder_1_out2, decoder_1_out3, decoder_1_out4, decoder_1_out5, decoder_1_out6,
       decoder_1_out7, decoder_1_out8, decoder_1_out9, decoder_1_out10, decoder_1_out11, decoder_1_out12,
       decoder_1_out13, decoder_1_out14, decoder_1_out15, decoder_1_out16, decoder_1_out17, decoder_1_out18,
       decoder_1_out19, decoder_1_out20, decoder_1_out21, decoder_1_out22, decoder_1_out23, decoder_1_out24,
       decoder_1_out25, decoder_1_out26, decoder_1_out27, decoder_1_out28, decoder_1_out29, decoder_1_out30,
       decoder_1_out31;
  wire [31:0] reg0_q, reg1_q, reg2_q, reg3_q, reg4_q, reg5_q, reg6_q, reg7_q, reg8_q, reg9_q, reg10_q,
       reg11_q, reg12_q, reg13_q, reg14_q, reg15_q, reg16_q, reg17_q, reg18_q, reg19_q, reg20_q, reg21_q,
       reg22_q, reg23_q, reg24_q, reg25_q, reg26_q, reg27_q, reg28_q, reg29_q, reg30_q, reg31_q;

  Decoder #(.enable("false"), .select(5)) decoder_1 (
    .out1(decoder_1_out1), .out2(decoder_1_out2), .out3(decoder_1_out3), .out4(decoder_1_out4),
    .out5(decoder_1_out5), .out6(decoder_1_out6), .out7(decoder_1_out7), .out8(decoder_1_out8),
    .out9(decoder_1_out9), .out10(decoder_1_out10), .out11(decoder_1_out11), .out12(decoder_1_out12),
    .out13(decoder_1_out13), .out14(decoder_1_out14), .out15(decoder_1_out15), .out16(decoder_1_out16),
    .out17(decoder_1_out17), .out18(decoder_1_out18), .out19(decoder_1_out19), .out20(decoder_1_out20),
    .out21(decoder_1_out21), .out22(decoder_1_out22), .out23(decoder_1_out23), .out24(decoder_1_out24),
    .out25(decoder_1_out25), .out26(decoder_1_out26), .out27(decoder_1_out27), .out28(decoder_1_out28),
    .out29(decoder_1_out29), .out30(decoder_1_out30), .out31(decoder_1_out31), .sel(reg_save));  // open: out0
  Register #(.width(32)) reg0 (.D(reg_in), .clk(clock), .Q(reg0_q));  // open: en, clr
  Register #(.width(32)) reg1 (.D(reg_in), .en(decoder_1_out1), .clk(clock), .Q(reg1_q));  // open: clr
  Register #(.width(32)) reg2 (.D(reg_in), .en(decoder_1_out2), .clk(clock), .Q(reg2_q));  // open: clr
  Register #(.width(32)) reg3 (.D(reg_in), .en(decoder_1_out3), .clk(clock), .Q(reg3_q));  // open: clr
  Register #(.width(32)) reg4 (.D(reg_in), .en(decoder_1_out4), .clk(clock), .Q(reg4_q));  // open: clr
  Register #(.width(32)) reg5 (.D(reg_in), .en(decoder_1_out5), .clk(clock), .Q(reg5_q));  // open: clr
  Register #(.width(32)) reg6 (.D(reg_in), .en(decoder_1_out6), .clk(clock), .Q(reg6_q));  // open: clr
  Register #(.width(32)) reg7 (.D(reg_in), .en(decoder_1_out7), .clk(clock), .Q(reg7_q));  // open: clr
  Register #(.width(32)) reg8 (.D(reg_in), .en(decoder_1_out8), .clk(clock), .Q(reg8_q));  // open: clr
  Register #(.width(32)) reg9 (.D(reg_in), .en(decoder_1_out9), .clk(clock), .Q(reg9_q));  // open: clr
  Register #(.width(32)) reg10 (.D(reg_in), .en(decoder_1_out10), .clk(clock), .Q(reg10_q));  // open: clr
  Register #(.width(32)) reg11 (.D(reg_in), .en(decoder_1_out11), .clk(clock), .Q(reg11_q));  // open: clr
  Register #(.width(32)) reg12 (.D(reg_in), .en(decoder_1_out12), .clk(clock), .Q(reg12_q));  // open: clr
  Register #(.width(32)) reg13 (.D(reg_in), .en(decoder_1_out13), .clk(clock), .Q(reg13_q));  // open: clr
  Register #(.width(32)) reg14 (.D(reg_in), .en(decoder_1_out14), .clk(clock), .Q(reg14_q));  // open: clr
  Register #(.width(32)) reg15 (.D(reg_in), .en(decoder_1_out15), .clk(clock), .Q(reg15_q));  // open: clr
  Register #(.width(32)) reg16 (.D(reg_in), .en(decoder_1_out16), .clk(clock), .Q(reg16_q));  // open: clr
  Register #(.width(32)) reg17 (.D(reg_in), .en(decoder_1_out17), .clk(clock), .Q(reg17_q));  // open: clr
  Register #(.width(32)) reg18 (.D(reg_in), .en(decoder_1_out18), .clk(clock), .Q(reg18_q));  // open: clr
  Register #(.width(32)) reg19 (.D(reg_in), .en(decoder_1_out19), .clk(clock), .Q(reg19_q));  // open: clr
  Register #(.width(32)) reg20 (.D(reg_in), .en(decoder_1_out20), .clk(clock), .Q(reg20_q));  // open: clr
  Register #(.width(32)) reg21 (.D(reg_in), .en(decoder_1_out21), .clk(clock), .Q(reg21_q));  // open: clr
  Register #(.width(32)) reg22 (.D(reg_in), .en(decoder_1_out22), .clk(clock), .Q(reg22_q));  // open: clr
  Register #(.width(32)) reg23 (.D(reg_in), .en(decoder_1_out23), .clk(clock), .Q(reg23_q));  // open: clr
  Register #(.width(32)) reg24 (.D(reg_in), .en(decoder_1_out24), .clk(clock), .Q(reg24_q));  // open: clr
  Register #(.width(32)) reg25 (.D(reg_in), .en(decoder_1_out25), .clk(clock), .Q(reg25_q));  // open: clr
  Register #(.width(32)) reg26 (.D(reg_in), .en(decoder_1_out26), .clk(clock), .Q(reg26_q));  // open: clr
  Register #(.width(32)) reg27 (.D(reg_in), .en(decoder_1_out27), .clk(clock), .Q(reg27_q));  // open: clr
  Register #(.width(32)) reg28 (.D(reg_in), .en(decoder_1_out28), .clk(clock), .Q(reg28_q));  // open: clr
  Register #(.width(32)) reg29 (.D(reg_in), .en(decoder_1_out29), .clk(clock), .Q(reg29_q));  // open: clr
  Register #(.width(32)) reg30 (.D(reg_in), .en(decoder_1_out30), .clk(clock), .Q(reg30_q));  // open: clr
  Register #(.width(32)) reg31 (.D(reg_in), .en(decoder_1_out31), .clk(clock), .Q(reg31_q));  // open: clr
  Multiplexer #(.select(5), .width(32)) multiplexer_1 (
    .in0(reg0_q), .in1(reg1_q), .in2(reg2_q), .in3(reg3_q), .in4(reg4_q), .in5(reg5_q), .in6(reg6_q),
    .in7(reg7_q), .in8(reg8_q), .in9(reg9_q), .in10(reg10_q), .in11(reg11_q), .in12(reg12_q), .in13(reg13_q),
    .in14(reg14_q), .in15(reg15_q), .in16(reg16_q), .in17(reg17_q), .in18(reg18_q), .in19(reg19_q),
    .in20(reg20_q), .in21(reg21_q), .in22(reg22_q), .in23(reg23_q), .in24(reg24_q), .in25(reg25_q),
    .in26(reg26_q), .in27(reg27_q), .in28(reg28_q), .in29(reg29_q), .in30(reg30_q), .in31(reg31_q),
    .out(reg_out_0), .sel(reg_load_0));
  Multiplexer #(.select(5), .width(32)) multiplexer_2 (
    .in0(reg0_q), .in1(reg1_q), .in2(reg2_q), .in3(reg3_q), .in4(reg4_q), .in5(reg5_q), .in6(reg6_q),
    .in7(reg7_q), .in8(reg8_q), .in9(reg9_q), .in10(reg10_q), .in11(reg11_q), .in12(reg12_q), .in13(reg13_q),
    .in14(reg14_q), .in15(reg15_q), .in16(reg16_q), .in17(reg17_q), .in18(reg18_q), .in19(reg19_q),
    .in20(reg20_q), .in21(reg21_q), .in22(reg22_q), .in23(reg23_q), .in24(reg24_q), .in25(reg25_q),
    .in26(reg26_q), .in27(reg27_q), .in28(reg28_q), .in29(reg29_q), .in30(reg30_q), .in31(reg31_q),
    .out(reg_out_1), .sel(reg_load_1));
endmodule
